// Logisim project POTATO_1_CPU.circ as structural Verilog: 10 circuits, main circuit main
module main (
);

  wire and_2_out, clock_1_out, controlled_buffer_1_out, decoder_1_out0, decoder_1_out1, decoder_1_out2,
       decoder_1_out3, decoder_1_out4, decoder_1_out5, decoder_1_out6, decoder_1_out7, decoder_1_out8,
       decoder_1_out9, decoder_1_out10, decoder_1_out11, decoder_1_out12, decoder_1_out13, decoder_1_out14,
       decoder_1_out15, not_1_out, RST_out, Stack_stackoverflow, undriven, vgagraphics_1_hpxl,
       vgagraphics_1_hsync, vgagraphics_1_vpxl, vgagraphics_1_vsync;
  wire [1:0] instructionregister_1_data_out_i_raw, vgagraphics_1_b, vgagraphics_1_g, vgagraphics_1_r;
  wire [3:0] alu_1_out_flags, instructionregister_1_data_out_istep;
  wire [7:0] alu_1_out_sum_raw, ARegister_data_out_raw, BRegister_data_out_raw, CRegister_data_out_raw,
       FlagsRegister_data_out_raw, RAM_data_out_raw, Stack_data_out, Stack_data_out_raw, Stack_out_sp_raw;
  wire [7:2] instructionregister_1_data_out_i_raw_2;
  wire [15:0] instructionregister_1_data_out_buf_raw, programcounter_1_data_out_raw, RAM_out_adr_raw;
  wire [31:0] controllogic_1_ctrl_word;

  Button RST (.out(RST_out));
  Clock clock_1 (.out(clock_1_out));
  LED led_1 (.in(Stack_stackoverflow));
  ByteStack Stack (
    .RST(RST_out), .CLK(controlled_buffer_1_out), .DATA_IN(Stack_data_out),
    .StackOverflow(Stack_stackoverflow), .OUT_SP_RAW(Stack_out_sp_raw), .DATA_OUT_RAW(Stack_data_out_raw),
    .DATA_OUT(Stack_data_out));  // open: INC, ENBL, LOAD, OUT_B
  DoubleByteRAM RAM (
    .RST(RST_out), .CLK(controlled_buffer_1_out), .DATA_IN(Stack_data_out), .OUT_ADR_RAW(RAM_out_adr_raw),
    .DATA_OUT_RAW(RAM_data_out_raw), .DATA_OUT_BUF(Stack_data_out));  // open: LOAD, LOAD_ADR_LB, LOAD_ADR_HB, OUT_B
  InstructionRegister instructionregister_1 (
    .DATA_IN(Stack_data_out), .RST(RST_out), .CLK(controlled_buffer_1_out),
    .DATA_OUT_I_RAW({instructionregister_1_data_out_i_raw_2, instructionregister_1_data_out_i_raw}),
    .DATA_OUT_BUF_RAW(instructionregister_1_data_out_buf_raw), .DATA_OUT_I_BUF(Stack_data_out),
    .DATA_OUT_BUF_LB_BUF(Stack_data_out), .DATA_OUT_BUF_HB_BUF(Stack_data_out),
    .DATA_OUT_ISTEP(instructionregister_1_data_out_istep));  // open: LOAD_I, OUT_BUF_LB, LOAD_BUF_LB, OUT_BUF_HB, LOAD_BUF_HB
  ControlLogic controllogic_1 (
    .INSTR(instructionregister_1_data_out_i_raw_2[7:4]), .INSTR_STEP(instructionregister_1_data_out_istep),
    .IMM_REG(instructionregister_1_data_out_i_raw_2[3]), .REG_ID(instructionregister_1_data_out_i_raw),
    .FLAGS(FlagsRegister_data_out_raw[3:0]), .MODE(instructionregister_1_data_out_i_raw_2[2]),
    .CTRL_WORD(controllogic_1_ctrl_word));
  LedBar SP (
    .led0(Stack_out_sp_raw[7]), .led1(Stack_out_sp_raw[6]), .led2(Stack_out_sp_raw[5]),
    .led3(Stack_out_sp_raw[4]), .led4(Stack_out_sp_raw[3]), .led5(Stack_out_sp_raw[2]),
    .led6(Stack_out_sp_raw[1]), .led7(Stack_out_sp_raw[0]));
  LedBar #(.matrixcols(16)) RAMAddress (
    .led0(RAM_out_adr_raw[15]), .led1(RAM_out_adr_raw[14]), .led2(RAM_out_adr_raw[13]),
    .led3(RAM_out_adr_raw[12]), .led4(RAM_out_adr_raw[11]), .led5(RAM_out_adr_raw[10]),
    .led6(RAM_out_adr_raw[9]), .led7(RAM_out_adr_raw[8]), .led8(RAM_out_adr_raw[7]),
    .led9(RAM_out_adr_raw[6]), .led10(RAM_out_adr_raw[5]), .led11(RAM_out_adr_raw[4]),
    .led12(RAM_out_adr_raw[3]), .led13(RAM_out_adr_raw[2]), .led14(RAM_out_adr_raw[1]),
    .led15(RAM_out_adr_raw[0]));
  LedBar Instruction (
    .led0(instructionregister_1_data_out_i_raw_2[7]), .led1(instructionregister_1_data_out_i_raw_2[6]),
    .led2(instructionregister_1_data_out_i_raw_2[5]), .led3(instructionregister_1_data_out_i_raw_2[4]),
    .led4(instructionregister_1_data_out_i_raw_2[3]), .led5(instructionregister_1_data_out_i_raw_2[2]),
    .led6(instructionregister_1_data_out_i_raw[1]), .led7(instructionregister_1_data_out_i_raw[0]));
  LedBar #(.matrixcols(4)) ledbar_1 (
    .led0(instructionregister_1_data_out_istep[3]), .led1(instructionregister_1_data_out_istep[2]),
    .led2(instructionregister_1_data_out_istep[1]), .led3(instructionregister_1_data_out_istep[0]));
  LedBar StackValue (
    .led0(Stack_data_out_raw[7]), .led1(Stack_data_out_raw[6]), .led2(Stack_data_out_raw[5]),
    .led3(Stack_data_out_raw[4]), .led4(Stack_data_out_raw[3]), .led5(Stack_data_out_raw[2]),
    .led6(Stack_data_out_raw[1]), .led7(Stack_data_out_raw[0]));
  LedBar #(.matrixcols(16)) InstructionBuffer (
    .led0(instructionregister_1_data_out_buf_raw[15]), .led1(instructionregister_1_data_out_buf_raw[14]),
    .led2(instructionregister_1_data_out_buf_raw[13]), .led3(instructionregister_1_data_out_buf_raw[12]),
    .led4(instructionregister_1_data_out_buf_raw[11]), .led5(instructionregister_1_data_out_buf_raw[10]),
    .led6(instructionregister_1_data_out_buf_raw[9]), .led7(instructionregister_1_data_out_buf_raw[8]),
    .led8(instructionregister_1_data_out_buf_raw[7]), .led9(instructionregister_1_data_out_buf_raw[6]),
    .led10(instructionregister_1_data_out_buf_raw[5]), .led11(instructionregister_1_data_out_buf_raw[4]),
    .led12(instructionregister_1_data_out_buf_raw[3]), .led13(instructionregister_1_data_out_buf_raw[2]),
    .led14(instructionregister_1_data_out_buf_raw[1]), .led15(instructionregister_1_data_out_buf_raw[0]));
  LedBar #(.matrixcols(16)) InstructionStep (
    .led0(decoder_1_out0), .led1(decoder_1_out1), .led2(decoder_1_out2), .led3(decoder_1_out3),
    .led4(decoder_1_out4), .led5(decoder_1_out5), .led6(decoder_1_out6), .led7(decoder_1_out7),
    .led8(decoder_1_out8), .led9(decoder_1_out9), .led10(decoder_1_out10), .led11(decoder_1_out11),
    .led12(decoder_1_out12), .led13(decoder_1_out13), .led14(decoder_1_out14), .led15(decoder_1_out15));
  Decoder #(.select(4)) decoder_1 (
    .out0(decoder_1_out0), .out1(decoder_1_out1), .out2(decoder_1_out2), .out3(decoder_1_out3),
    .out4(decoder_1_out4), .out5(decoder_1_out5), .out6(decoder_1_out6), .out7(decoder_1_out7),
    .out8(decoder_1_out8), .out9(decoder_1_out9), .out10(decoder_1_out10), .out11(decoder_1_out11),
    .out12(decoder_1_out12), .out13(decoder_1_out13), .out14(decoder_1_out14), .out15(decoder_1_out15),
    .sel(instructionregister_1_data_out_istep));  // open: en
  LedBar RAMValue (
    .led0(RAM_data_out_raw[7]), .led1(RAM_data_out_raw[6]), .led2(RAM_data_out_raw[5]),
    .led3(RAM_data_out_raw[4]), .led4(RAM_data_out_raw[3]), .led5(RAM_data_out_raw[2]),
    .led6(RAM_data_out_raw[1]), .led7(RAM_data_out_raw[0]));
  assign controlled_buffer_1_out = not_1_out ? clock_1_out : 1'bz;  // Controlled_Buffer controlled_buffer_1
  not not_1 (not_1_out, controllogic_1_ctrl_word[31]);
  LedBar #(.matrixcols(32)) ControlWord (
    .led0(controllogic_1_ctrl_word[31]), .led1(controllogic_1_ctrl_word[30]),
    .led2(controllogic_1_ctrl_word[29]), .led3(controllogic_1_ctrl_word[28]),
    .led4(controllogic_1_ctrl_word[27]), .led5(controllogic_1_ctrl_word[26]),
    .led6(controllogic_1_ctrl_word[25]), .led7(controllogic_1_ctrl_word[24]),
    .led8(controllogic_1_ctrl_word[23]), .led9(controllogic_1_ctrl_word[22]),
    .led10(controllogic_1_ctrl_word[21]), .led11(controllogic_1_ctrl_word[20]),
    .led12(controllogic_1_ctrl_word[19]), .led13(controllogic_1_ctrl_word[18]),
    .led14(controllogic_1_ctrl_word[17]), .led15(controllogic_1_ctrl_word[16]),
    .led16(controllogic_1_ctrl_word[15]), .led17(controllogic_1_ctrl_word[14]),
    .led18(controllogic_1_ctrl_word[13]), .led19(controllogic_1_ctrl_word[12]),
    .led20(controllogic_1_ctrl_word[11]), .led21(controllogic_1_ctrl_word[10]),
    .led22(controllogic_1_ctrl_word[9]), .led23(controllogic_1_ctrl_word[8]),
    .led24(controllogic_1_ctrl_word[7]), .led25(controllogic_1_ctrl_word[6]),
    .led26(controllogic_1_ctrl_word[5]), .led27(controllogic_1_ctrl_word[4]),
    .led28(controllogic_1_ctrl_word[3]), .led29(controllogic_1_ctrl_word[2]),
    .led30(controllogic_1_ctrl_word[1]), .led31(controllogic_1_ctrl_word[0]));
  LedBar BUS_OUT (
    .led0(Stack_data_out[7]), .led1(Stack_data_out[6]), .led2(Stack_data_out[5]), .led3(Stack_data_out[4]),
    .led4(Stack_data_out[3]), .led5(Stack_data_out[2]), .led6(Stack_data_out[1]), .led7(Stack_data_out[0]));
  Pull_Resistor pull_resistor_1 (.node(Stack_data_out[7]));
  Pull_Resistor pull_resistor_2 (.node(Stack_data_out[6]));
  Pull_Resistor pull_resistor_3 (.node(Stack_data_out[5]));
  Pull_Resistor pull_resistor_4 (.node(Stack_data_out[4]));
  Pull_Resistor pull_resistor_5 (.node(Stack_data_out[3]));
  Pull_Resistor pull_resistor_6 (.node(Stack_data_out[2]));
  Pull_Resistor pull_resistor_7 (.node(Stack_data_out[1]));
  Pull_Resistor pull_resistor_8 (.node(Stack_data_out[0]));
  and and_1 (controllogic_1_ctrl_word[31], undriven, and_2_out);
  and and_2 (and_2_out, vgagraphics_1_hpxl, vgagraphics_1_vpxl);
  LedBar #(.matrixcols(16)) PC (
    .led0(programcounter_1_data_out_raw[15]), .led1(programcounter_1_data_out_raw[14]),
    .led2(programcounter_1_data_out_raw[13]), .led3(programcounter_1_data_out_raw[12]),
    .led4(programcounter_1_data_out_raw[11]), .led5(programcounter_1_data_out_raw[10]),
    .led6(programcounter_1_data_out_raw[9]), .led7(programcounter_1_data_out_raw[8]),
    .led8(programcounter_1_data_out_raw[7]), .led9(programcounter_1_data_out_raw[6]),
    .led10(programcounter_1_data_out_raw[5]), .led11(programcounter_1_data_out_raw[4]),
    .led12(programcounter_1_data_out_raw[3]), .led13(programcounter_1_data_out_raw[2]),
    .led14(programcounter_1_data_out_raw[1]), .led15(programcounter_1_data_out_raw[0]));
  ProgramCounter programcounter_1 (
    .RST(RST_out), .CLK(controlled_buffer_1_out), .DATA_IN(Stack_data_out),
    .DATA_OUT_RAW(programcounter_1_data_out_raw), .DATA_OUT_BUF(Stack_data_out));  // open: OUT_LB, OUT_HB, LOAD_LB, LOAD_HB, ENBL, CRY
  LedBar ledbar_2 (
    .led0(ARegister_data_out_raw[7]), .led1(ARegister_data_out_raw[6]), .led2(ARegister_data_out_raw[5]),
    .led3(ARegister_data_out_raw[4]), .led4(ARegister_data_out_raw[3]), .led5(ARegister_data_out_raw[2]),
    .led6(ARegister_data_out_raw[1]), .led7(ARegister_data_out_raw[0]));
  ByteRegister ARegister (
    .DATA_IN(Stack_data_out), .CLK(controlled_buffer_1_out), .RST(RST_out),
    .DATA_OUT_RAW(ARegister_data_out_raw), .DATA_OUT_BUF(Stack_data_out));  // open: OUT_B, LOAD
  LedBar ledbar_3 (
    .led0(BRegister_data_out_raw[7]), .led1(BRegister_data_out_raw[6]), .led2(BRegister_data_out_raw[5]),
    .led3(BRegister_data_out_raw[4]), .led4(BRegister_data_out_raw[3]), .led5(BRegister_data_out_raw[2]),
    .led6(BRegister_data_out_raw[1]), .led7(BRegister_data_out_raw[0]));
  ByteRegister BRegister (
    .DATA_IN(Stack_data_out), .CLK(controlled_buffer_1_out), .RST(RST_out),
    .DATA_OUT_RAW(BRegister_data_out_raw), .DATA_OUT_BUF(Stack_data_out));  // open: OUT_B, LOAD
  LedBar ledbar_4 (
    .led0(CRegister_data_out_raw[7]), .led1(CRegister_data_out_raw[6]), .led2(CRegister_data_out_raw[5]),
    .led3(CRegister_data_out_raw[4]), .led4(CRegister_data_out_raw[3]), .led5(CRegister_data_out_raw[2]),
    .led6(CRegister_data_out_raw[1]), .led7(CRegister_data_out_raw[0]));
  ByteRegister CRegister (
    .DATA_IN(Stack_data_out), .CLK(controlled_buffer_1_out), .RST(RST_out),
    .DATA_OUT_RAW(CRegister_data_out_raw), .DATA_OUT_BUF(Stack_data_out));  // open: OUT_B, LOAD
  LedBar SUM (
    .led0(alu_1_out_sum_raw[7]), .led1(alu_1_out_sum_raw[6]), .led2(alu_1_out_sum_raw[5]),
    .led3(alu_1_out_sum_raw[4]), .led4(alu_1_out_sum_raw[3]), .led5(alu_1_out_sum_raw[2]),
    .led6(alu_1_out_sum_raw[1]), .led7(alu_1_out_sum_raw[0]));
  ALU alu_1 (
    .OUT_SUM_RAW(alu_1_out_sum_raw), .OUT_SUM_BUF(Stack_data_out), .OUT_FLAGS(alu_1_out_flags));  // open: IN_A, IN_B, IN_CRY, SUB, OUT_B
  VGAGraphics vgagraphics_1 (
    .DATA_IN(Stack_data_out), .VRAM_LOAD(undriven), .CPU_CLK(controlled_buffer_1_out), .CPU_RST(RST_out),
    .HPXL(vgagraphics_1_hpxl), .HSYNC(vgagraphics_1_hsync), .VPXL(vgagraphics_1_vpxl),
    .VSYNC(vgagraphics_1_vsync), .R(vgagraphics_1_r), .G(vgagraphics_1_g), .B(vgagraphics_1_b));  // open: LOAD_ADR_LB, LOAD_ADR_HB
  ByteRegister FlagsRegister (
    .DATA_IN({4'b0000, alu_1_out_flags}), .CLK(controlled_buffer_1_out), .RST(RST_out),
    .DATA_OUT_RAW(FlagsRegister_data_out_raw));  // open: OUT_B, LOAD, DATA_OUT_BUF
  LedBar #(.matrixcols(4)) L_E_C_Z (
    .led0(FlagsRegister_data_out_raw[3]), .led1(FlagsRegister_data_out_raw[2]),
    .led2(FlagsRegister_data_out_raw[1]), .led3(FlagsRegister_data_out_raw[0]));
  // SocVga #(.DisplayMode("800x600"), .SocBusSelection('h0000017FA811F07E6ababd23), .soft160x120("false"), .soft320x240("false"), .soft640x480("false"), .soft800x600("true")) socvga_1: pin names not known
  // SocBus #(.SocBusIdentifier('h0000017FA811F07E6ababd23)) socbus_1: pin names not known; wires that end beside it: RST_out
  // RGB_Video #(.cursor("No Cursor"), .height(256), .width(256)) rgb_video_1: pin names not known
endmodule

module ByteCounter (
  input  LOAD,
  input  INC,
  input  ENBL,
  input  RST,
  input  CLK,
  input  [7:0] DATA_IN,
  output CRY,
  output [7:0] DATA_OUT
);

  Counter counter_1 (.clr(RST), .load(LOAD), .up(INC), .count(ENBL), .clk(CLK), .D(DATA_IN), .carry(CRY), .Q(DATA_OUT));
endmodule

module ProgramCounter (
  input  OUT_LB,
  input  OUT_HB,
  input  LOAD_LB,
  input  LOAD_HB,
  input  ENBL,
  input  RST,
  input  CLK,
  input  [7:0] DATA_IN,
  output [15:0] DATA_OUT_RAW,
  output [7:0] DATA_OUT_BUF,
  output CRY
);

  wire LBCounter_cry;

  ByteCounter LBCounter (
    .LOAD(LOAD_LB), .INC(1'b1), .ENBL(ENBL), .RST(RST), .CLK(CLK), .DATA_IN(DATA_IN), .CRY(LBCounter_cry),
    .DATA_OUT(DATA_OUT_RAW[7:0]));
  assign DATA_OUT_BUF = OUT_LB ? DATA_OUT_RAW[7:0] : 8'bz;  // Controlled_Buffer controlled_buffer_1
  assign DATA_OUT_BUF = OUT_HB ? DATA_OUT_RAW[15:8] : 8'bz;  // Controlled_Buffer controlled_buffer_2
  ByteCounter HBCounter (
    .LOAD(LOAD_HB), .INC(1'b1), .ENBL(LBCounter_cry), .RST(RST), .CLK(CLK), .DATA_IN(DATA_IN), .CRY(CRY),
    .DATA_OUT(DATA_OUT_RAW[15:8]));
endmodule

module ByteRegister (
  input  [7:0] DATA_IN,
  input  OUT_B,
  input  LOAD,
  input  CLK,
  input  RST,
  output [7:0] DATA_OUT_RAW,
  output [7:0] DATA_OUT_BUF
);

  Register register_1 (.D(DATA_IN), .en(LOAD), .clk(CLK), .Q(DATA_OUT_RAW), .clr(RST));
  assign DATA_OUT_BUF = OUT_B ? DATA_OUT_RAW : 8'bz;  // Controlled_Buffer controlled_buffer_1
endmodule

module InstructionRegister (
  input  [7:0] DATA_IN,
  input  LOAD_I,
  input  OUT_BUF_LB,
  input  LOAD_BUF_LB,
  input  OUT_BUF_HB,
  input  LOAD_BUF_HB,
  input  RST,
  input  CLK,
  output [7:0] DATA_OUT_I_RAW,
  output [15:0] DATA_OUT_BUF_RAW,
  output [7:0] DATA_OUT_I_BUF,
  output [7:0] DATA_OUT_BUF_LB_BUF,
  output [7:0] DATA_OUT_BUF_HB_BUF,
  output [3:0] DATA_OUT_ISTEP
);

  wire or_1_out;
  wire [7:4] StepCounter_data_out;

  or or_1 (or_1_out, RST, StepCounter_data_out[4]);
  ByteRegister IRegister (
    .DATA_IN(DATA_IN), .LOAD(LOAD_I), .CLK(CLK), .RST(RST), .DATA_OUT_RAW(DATA_OUT_I_RAW),
    .DATA_OUT_BUF(DATA_OUT_I_BUF));  // open: OUT_B
  ByteCounter StepCounter (
    .INC(1'b1), .ENBL(1'b1), .RST(or_1_out), .CLK(CLK), .DATA_OUT({StepCounter_data_out, DATA_OUT_ISTEP}));  // open: LOAD, DATA_IN, CRY
  ByteRegister BufferLB (
    .DATA_IN(DATA_IN), .OUT_B(OUT_BUF_LB), .LOAD(LOAD_BUF_LB), .CLK(CLK), .RST(RST),
    .DATA_OUT_RAW(DATA_OUT_BUF_RAW[7:0]), .DATA_OUT_BUF(DATA_OUT_BUF_LB_BUF));
  ByteRegister BufferHB (
    .DATA_IN(DATA_IN), .OUT_B(OUT_BUF_HB), .LOAD(LOAD_BUF_HB), .CLK(CLK), .RST(RST),
    .DATA_OUT_RAW(DATA_OUT_BUF_RAW[15:8]), .DATA_OUT_BUF(DATA_OUT_BUF_HB_BUF));
endmodule

module ByteStack (
  input  INC,
  input  ENBL,
  input  LOAD,
  input  OUT_B,
  input  RST,
  input  CLK,
  input  [7:0] DATA_IN,
  output StackOverflow,
  output [7:0] OUT_SP_RAW,
  output [7:0] DATA_OUT_RAW,
  output [7:0] DATA_OUT
);

  RAM #(.enables("line")) Stack (.addr(OUT_SP_RAW), .we(LOAD), .clk(CLK), .din(DATA_IN), .dout(DATA_OUT_RAW));
  ByteCounter StackPointer (
    .INC(INC), .ENBL(ENBL), .RST(RST), .CLK(CLK), .CRY(StackOverflow), .DATA_OUT(OUT_SP_RAW));  // open: LOAD, DATA_IN
  assign DATA_OUT = OUT_B ? DATA_OUT_RAW : 8'bz;  // Controlled_Buffer controlled_buffer_1
endmodule

module DoubleByteRAM (
  input  LOAD,
  input  LOAD_ADR_LB,
  input  LOAD_ADR_HB,
  input  OUT_B,
  input  RST,
  input  CLK,
  input  [7:0] DATA_IN,
  output [15:0] OUT_ADR_RAW,
  output [7:0] DATA_OUT_RAW,
  output [7:0] DATA_OUT_BUF
);

  ByteRegister AddressRegisterLB (
    .DATA_IN(DATA_IN), .LOAD(LOAD_ADR_LB), .CLK(CLK), .RST(RST), .DATA_OUT_RAW(OUT_ADR_RAW[7:0]));  // open: OUT_B, DATA_OUT_BUF
  ByteRegister AddressRegisterHB (
    .DATA_IN(DATA_IN), .LOAD(LOAD_ADR_HB), .CLK(CLK), .RST(RST), .DATA_OUT_RAW(OUT_ADR_RAW[15:8]));  // open: OUT_B, DATA_OUT_BUF
  RAM #(.addrWidth(16), .enables("line")) ram_1 (
    .addr(OUT_ADR_RAW), .we(LOAD), .clk(CLK), .din(DATA_IN), .dout(DATA_OUT_RAW));
  assign DATA_OUT_BUF = OUT_B ? DATA_OUT_RAW : 8'bz;  // Controlled_Buffer controlled_buffer_1
endmodule

module ALU (
  input  [7:0] IN_A,
  input  [7:0] IN_B,
  input  IN_CRY,
  input  SUB,
  input  OUT_B,
  output [7:0] OUT_SUM_RAW,
  output [7:0] OUT_SUM_BUF,
  output [3:0] OUT_FLAGS
);

  wire and_1_out, and_3_out, nor_1_out, nor_2_out, nor_3_out, nor_4_out, or_1_out;
  wire [7:0] xor_1_out;

  assign xor_1_out = IN_B ^ {8{SUB}};  // XOR_Gate xor_1, 8 bits wide
  or or_1 (or_1_out, IN_CRY, SUB);
  Adder adder_1 (.a(IN_A), .b(xor_1_out), .out(OUT_SUM_RAW), .cin(or_1_out), .cout(OUT_FLAGS[1]));
  nor nor_1 (nor_1_out, OUT_SUM_RAW[7], OUT_SUM_RAW[6]);
  nor nor_2 (nor_2_out, OUT_SUM_RAW[5], OUT_SUM_RAW[4]);
  and and_1 (and_1_out, nor_1_out, nor_2_out);
  and and_2 (OUT_FLAGS[0], and_1_out, and_3_out);
  nor nor_3 (nor_3_out, OUT_SUM_RAW[3], OUT_SUM_RAW[2]);
  nor nor_4 (nor_4_out, OUT_SUM_RAW[1], OUT_SUM_RAW[0]);
  and and_3 (and_3_out, nor_3_out, nor_4_out);
  Comparator comparator_1 (.a(IN_A), .b(IN_B), .eq(OUT_FLAGS[2]), .lt(OUT_FLAGS[3]));  // open: gt
  assign OUT_SUM_BUF = OUT_B ? OUT_SUM_RAW : 8'bz;  // Controlled_Buffer controlled_buffer_1

  // Notes on the sheet:
  //   ZERO
endmodule

module ControlLogic (
  input  [3:0] INSTR,
  input  [3:0] INSTR_STEP,
  input  IMM_REG,
  input  [1:0] REG_ID,
  input  [3:0] FLAGS,
  input  MODE,
  output [31:0] CTRL_WORD
);

  ROM #(.addrWidth(16), .dataWidth(32)) rom_1 (
    .addr({MODE, FLAGS, REG_ID, IMM_REG, INSTR_STEP, INSTR}), .data(CTRL_WORD));
endmodule

module VGAGraphics (
  input  [7:0] DATA_IN,
  input  VRAM_LOAD,
  input  LOAD_ADR_LB,
  input  LOAD_ADR_HB,
  input  CPU_CLK,
  input  CPU_RST,
  output HPXL,
  output HSYNC,
  output VPXL,
  output VSYNC,
  output [1:0] R,
  output [1:0] G,
  output [1:0] B
);

  wire CLK_out, comparator_1_eq, comparator_2_eq, comparator_3_eq, comparator_4_eq, comparator_5_eq,
       comparator_6_eq, comparator_7_eq, comparator_8_eq, not_1_out, not_2_out, not_3_out, or_1_out,
       or_2_out, or_3_out, RST_out;
  wire [1:0] VRAM_dout;
  wire [7:0] undriven, undriven_2, VCounter_q, VRAM_ADR_HB_data_out_raw, VRAM_ADR_LB_data_out_raw;
  wire [8:2] HCounter_q;
  wire [15:0] controlled_buffer_1_out;

  Button RST (.out(RST_out));
  Clock CLK (.out(CLK_out));
  Counter #(.max('h1ff), .width(9)) HCounter (
    .clr(or_1_out), .load(1'b0), .up(1'b1), .count(1'b1), .clk(CLK_out),
    .Q({HCounter_q[8], undriven[7], HCounter_q[6:5], undriven[4:3], HCounter_q[2], undriven[1:0]}));  // open: D, carry
  or or_1 (or_1_out, RST_out, comparator_7_eq);
  Counter #(.max('h3ff), .width(10)) VCounter (
    .clr(or_2_out), .load(1'b0), .up(1'b1), .count(1'b1), .clk(comparator_7_eq),
    .Q({undriven_2[7:6], VCounter_q[7], undriven_2[4:3], VCounter_q[4], undriven_2[1:0], VCounter_q[1:0]}));  // open: D, carry
  or or_2 (or_2_out, RST_out, comparator_8_eq);
  ByteRegister VRAM_ADR_LB (
    .DATA_IN(DATA_IN), .LOAD(LOAD_ADR_LB), .CLK(CPU_CLK), .RST(CPU_RST),
    .DATA_OUT_RAW(VRAM_ADR_LB_data_out_raw));  // open: OUT_B, DATA_OUT_BUF
  ByteRegister VRAM_ADR_HB (
    .DATA_IN(DATA_IN), .LOAD(LOAD_ADR_HB), .CLK(CPU_CLK), .RST(CPU_RST),
    .DATA_OUT_RAW(VRAM_ADR_HB_data_out_raw));  // open: OUT_B, DATA_OUT_BUF
  Comparator #(.mode("unsigned"), .width(9)) comparator_1 (
    .a({HCounter_q[8], undriven[7], HCounter_q[6:5], undriven[4:3], HCounter_q[2], undriven[1:0]}),
    .b(9'hc8), .eq(comparator_1_eq));  // open: gt, lt
  Comparator #(.mode("unsigned"), .width(10)) comparator_2 (
    .a({undriven_2[7:6], VCounter_q[7], undriven_2[4:3], VCounter_q[4], undriven_2[1:0], VCounter_q[1:0]}),
    .b(10'h258), .eq(comparator_2_eq));  // open: gt, lt
  not not_1 (not_1_out, or_3_out);
  assign controlled_buffer_1_out = not_1_out ? {undriven_2, undriven} : 16'bz;  // Controlled_Buffer controlled_buffer_1
  RAM #(.addrWidth(16), .enables("line")) VRAM (
    .addr(controlled_buffer_1_out), .we(VRAM_LOAD), .clk(CPU_CLK), .din(DATA_IN), .dout({VRAM_dout, B, G, R}));
  assign controlled_buffer_1_out = or_3_out ? {VRAM_ADR_HB_data_out_raw, VRAM_ADR_LB_data_out_raw} : 16'bz;  // Controlled_Buffer controlled_buffer_2
  or or_3 (or_3_out, not_2_out, not_3_out);
  Comparator #(.mode("unsigned"), .width(9)) comparator_3 (
    .a({HCounter_q[8], undriven[7], HCounter_q[6:5], undriven[4:3], HCounter_q[2], undriven[1:0]}),
    .b(9'hd2), .eq(comparator_3_eq));  // open: gt, lt
  Comparator #(.mode("unsigned"), .width(10)) comparator_4 (
    .a({undriven_2[7:6], VCounter_q[7], undriven_2[4:3], VCounter_q[4], undriven_2[1:0], VCounter_q[1:0]}),
    .b(10'h259), .eq(comparator_4_eq));  // open: gt, lt
  not not_2 (not_2_out, VPXL);
  not not_3 (not_3_out, HPXL);
  Comparator #(.mode("unsigned"), .width(9)) comparator_5 (
    .a({HCounter_q[8], undriven[7], HCounter_q[6:5], undriven[4:3], HCounter_q[2], undriven[1:0]}),
    .b(9'hf2), .eq(comparator_5_eq));  // open: gt, lt
  Comparator #(.mode("unsigned"), .width(10)) comparator_6 (
    .a({undriven_2[7:6], VCounter_q[7], undriven_2[4:3], VCounter_q[4], undriven_2[1:0], VCounter_q[1:0]}),
    .b(10'h25d), .eq(comparator_6_eq));  // open: gt, lt
  Comparator #(.mode("unsigned"), .width(9)) comparator_7 (
    .a({HCounter_q[8], undriven[7], HCounter_q[6:5], undriven[4:3], HCounter_q[2], undriven[1:0]}),
    .b(9'h108), .eq(comparator_7_eq));  // open: gt, lt
  S_R_Flip_Flop HPXL_SR (
    .S(comparator_7_eq), .R(comparator_1_eq), .clk(CLK_out), .Q(HPXL), .reset(RST_out));  // open: Qn, preset
  S_R_Flip_Flop HSYNC_SR (
    .S(comparator_3_eq), .R(comparator_5_eq), .clk(CLK_out), .Q(HSYNC), .reset(RST_out));  // open: Qn, preset
  Comparator #(.mode("unsigned"), .width(10)) comparator_8 (
    .a({undriven_2[7:6], VCounter_q[7], undriven_2[4:3], VCounter_q[4], undriven_2[1:0], VCounter_q[1:0]}),
    .b(10'h274), .eq(comparator_8_eq));  // open: gt, lt
  S_R_Flip_Flop VPXL_SR (
    .S(comparator_8_eq), .R(comparator_2_eq), .clk(CLK_out), .Q(VPXL), .reset(RST_out));  // open: Qn, preset
  S_R_Flip_Flop VSYNC_SR (
    .S(comparator_4_eq), .R(comparator_6_eq), .clk(CLK_out), .Q(VSYNC), .reset(RST_out));  // open: Qn, preset

  // Notes on the sheet:
  //   200
  //   600
  //   210
  //   601
  //   242
  //   605
  //   264
  //   628
endmodule
